// Logisim project alu.circ as structural Verilog: 1 circuit, main circuit alu
module alu (
  input  [31:0] A,
  input  [31:0] B,
  input  [3:0] ALUSel,
  output [31:0] Result
);

  wire comparator_1_lt;
  wire [31:0] sel0, sel1, sel2, sel3, sel4, sel5, sel6, sel7, sel10, sel11, sel12, sel14;

  Adder #(.width(32)) adder_1 (.a(A), .b(B), .out(sel0));  // open: cin, cout
  Multiplier #(.mode("twosComplement"), .width(32)) multiplier_1 (
    .a(A), .b(B), .out(sel10), .cout(sel14));  // open: cin
  Multiplier #(.width(32)) multiplier_2 (.a(A), .b(B), .cout(sel11));  // open: out, cin
  assign sel1 = A & B;  // AND_Gate and_1, 32 bits wide
  Subtractor #(.width(32)) subtractor_1 (.a(A), .b(B), .out(sel12));  // open: bin, bout
  Multiplexer #(.enable("false"), .select(4), .width(32)) multiplexer_1 (
    .in0(sel0), .in1(sel1), .in2(sel2), .in3(sel3), .in4(sel4), .in5(sel5), .in6(sel6), .in7(sel7),
    .in10(sel10), .in11(sel11), .in12(sel12), .in13(B), .in14(sel14), .out(Result), .sel(ALUSel));  // open: in8, in9, in15
  assign sel2 = A | B;  // OR_Gate or_1, 32 bits wide
  assign sel3 = A ^ B;  // XOR_Gate xor_1, 32 bits wide
  Shifter #(.shift("lr"), .width(32)) shifter_1 (.in(A), .\dist (B[4:0]), .out(sel4));
  Shifter #(.shift("ar"), .width(32)) shifter_2 (.in(A), .\dist (B[4:0]), .out(sel5));
  Shifter #(.width(32)) shifter_3 (.in(A), .\dist (B[4:0]), .out(sel6));
  Comparator #(.width(32)) comparator_1 (.a(A), .b(B), .lt(comparator_1_lt));  // open: gt, eq
  assign sel7 = {{31{1'b0}}, comparator_1_lt};  // Bit_Extender bit_extender_1

  // Other names for the same wires on the sheet: sel13[31:0] = B

  // Notes on the sheet:
  //   14. MULH
  //   INPUTS to your circuit
  //   0. ADD
  //   10. MUL
  //   1. AND
  //   11. MULHU
  //   12. SUB
  //   DON'T CHANGE THE LOCATIONS OF THE INPUTS AND OUTPUTS!
  //   2. OR
  //   13. BSEL
  //   3. XOR
  //   4. SRL
  //   OUTPUT from your circuit
  //   5. SRA
  //   6. SLL
  //   7. SLT
  //   8. UNUSED
  //   9. UNUSED
endmodule
