// Logisim project control_logic.circ as structural Verilog: 1 circuit, main circuit control_logic
module control_logic (
  input  [31:0] inst,
  input  BrEq,
  input  BrLt,
  output PCSel,
  output RegWEn,
  output [2:0] ImmSel,
  output BrUn,
  output ASel,
  output BSel,
  output [3:0] ALUSel,
  output MemRW,
  output [1:0] WBSel,
  output CSRSel,
  output CSRWen
);

  wire and_7_out, and_8_out, and_9_out, and_10_out, and_11_out, and_12_out, and_13_out, comparator_1_eq,
       comparator_2_eq, comparator_4_eq, comparator_5_eq, comparator_6_eq, comparator_7_eq, comparator_8_eq,
       comparator_9_eq, comparator_10_eq, comparator_11_eq, comparator_12_eq, comparator_13_eq,
       comparator_15_eq, comparator_16_eq, comparator_17_eq, comparator_18_eq, comparator_19_eq,
       comparator_20_eq, comparator_21_eq, comparator_22_eq, comparator_23_eq, comparator_24_eq,
       comparator_25_eq, comparator_26_eq, comparator_27_eq, comparator_29_eq, comparator_30_eq,
       comparator_32_eq, comparator_33_eq, comparator_35_eq, comparator_36_eq, comparator_37_eq,
       comparator_38_eq, comparator_39_eq, comparator_40_eq, comparator_41_eq, comparator_42_eq,
       comparator_43_eq, comparator_44_eq, comparator_45_eq, comparator_46_eq, comparator_47_eq,
       comparator_48_eq, comparator_49_eq, comparator_50_eq, comparator_51_eq, comparator_52_eq,
       comparator_53_eq, comparator_54_eq, comparator_55_eq, comparator_56_eq, ImmSel_B, ImmSel_J, ImmSel_U,
       is_Mul, is_Mulh, is_Sra, is_Sub, not_1_out, not_2_out, not_3_out, or_4_out, or_5_out, or_9_out,
       WBSel_ALU, WBSel_Imm, WBSel_PC4;
  wire [1:0] multiplexer_1_out, multiplexer_2_out;
  wire [2:0] multiplexer_10_out, multiplexer_11_out, multiplexer_12_out, multiplexer_13_out;
  wire [3:0] ALUSel_IR, multiplexer_3_out, multiplexer_5_out, multiplexer_6_out, multiplexer_7_out;

  Comparator #(.mode("unsigned"), .width(7)) comparator_1 (
    .a(inst[6:0]), .b(7'b1101111), .eq(comparator_1_eq));  // open: gt, lt
  Comparator #(.mode("unsigned"), .width(7)) comparator_2 (
    .a(inst[6:0]), .b(7'b1100111), .eq(comparator_2_eq));  // open: gt, lt
  Comparator #(.mode("unsigned"), .width(7)) comparator_3 (
    .a(inst[6:0]), .b(7'b0110111), .eq(WBSel_Imm));  // open: gt, lt
  Comparator #(.mode("unsigned"), .width(7)) comparator_4 (
    .a(inst[6:0]), .b(7'b0110011), .eq(comparator_4_eq));  // open: gt, lt
  Comparator #(.mode("unsigned"), .width(7)) comparator_5 (
    .a(inst[6:0]), .b(7'b0010011), .eq(comparator_5_eq));  // open: gt, lt
  Comparator #(.mode("unsigned"), .width(7)) comparator_6 (
    .a(inst[6:0]), .b(7'b0010111), .eq(comparator_6_eq));  // open: gt, lt
  Multiplexer #(.enable("false"), .width(2)) multiplexer_1 (
    .in0(2'b00), .in1(2'b01), .out(multiplexer_1_out), .sel(WBSel_ALU));
  or or_1 (WBSel_PC4, comparator_1_eq, comparator_2_eq);
  or or_2 (WBSel_ALU, comparator_4_eq, comparator_5_eq, comparator_6_eq);
  Multiplexer #(.enable("false"), .width(2)) multiplexer_2 (
    .in0(multiplexer_1_out), .in1(2'b10), .out(multiplexer_2_out), .sel(WBSel_PC4));
  Comparator #(.mode("unsigned"), .width(7)) comparator_7 (
    .a(inst[6:0]), .b(7'b0110011), .eq(comparator_7_eq));  // open: gt, lt
  Comparator #(.mode("unsigned"), .width(7)) comparator_8 (
    .a(inst[6:0]), .b(7'b0000011), .eq(comparator_8_eq));  // open: gt, lt
  Comparator #(.mode("unsigned"), .width(7)) comparator_9 (
    .a(inst[6:0]), .b(7'b0010011), .eq(comparator_9_eq));  // open: gt, lt
  Comparator #(.mode("unsigned"), .width(7)) comparator_10 (
    .a(inst[6:0]), .b(7'b1100111), .eq(comparator_10_eq));  // open: gt, lt
  Comparator #(.mode("unsigned"), .width(7)) comparator_11 (
    .a(inst[6:0]), .b(7'b1101111), .eq(comparator_11_eq));  // open: gt, lt
  Comparator #(.mode("unsigned"), .width(7)) comparator_12 (
    .a(inst[6:0]), .b(7'b0010111), .eq(comparator_12_eq));  // open: gt, lt
  Comparator #(.mode("unsigned"), .width(7)) comparator_13 (
    .a(inst[6:0]), .b(7'b0110111), .eq(comparator_13_eq));  // open: gt, lt
  Comparator #(.mode("unsigned"), .width(7)) comparator_14 (
    .a(inst[6:0]), .b(7'b1110011), .eq(CSRWen));  // open: gt, lt
  Multiplexer #(.enable("false"), .select(3), .width(4)) multiplexer_3 (
    .in0(4'b0000), .in1(4'b0110), .in2(4'b0111), .in3(4'b1011), .in4(4'b0011), .in5(4'b0100), .in6(4'b0010),
    .in7(4'b0001), .out(multiplexer_3_out), .sel(inst[14:12]));
  Comparator #(.mode("unsigned"), .width(7)) comparator_15 (
    .a(inst[6:0]), .b(7'b0110011), .eq(comparator_15_eq));  // open: gt, lt
  Comparator #(.mode("unsigned"), .width(3)) comparator_16 (
    .a(inst[14:12]), .b(3'b000), .eq(comparator_16_eq));  // open: gt, lt
  Comparator #(.mode("unsigned"), .width(7)) comparator_17 (
    .a(inst[31:25]), .b(7'b0000001), .eq(comparator_17_eq));  // open: gt, lt
  Comparator #(.mode("unsigned"), .width(7)) comparator_18 (
    .a(inst[6:0]), .b(7'b0110011), .eq(comparator_18_eq));  // open: gt, lt
  Comparator #(.mode("unsigned"), .width(3)) comparator_19 (
    .a(inst[14:12]), .b(3'b000), .eq(comparator_19_eq));  // open: gt, lt
  Comparator #(.mode("unsigned"), .width(7)) comparator_20 (
    .a(inst[31:25]), .b(7'b0000010), .eq(comparator_20_eq));  // open: gt, lt
  Comparator #(.mode("unsigned"), .width(7)) comparator_21 (
    .a(inst[6:0]), .b(7'b0110011), .eq(comparator_21_eq));  // open: gt, lt
  Comparator #(.mode("unsigned"), .width(3)) comparator_22 (
    .a(inst[14:12]), .b(3'b001), .eq(comparator_22_eq));  // open: gt, lt
  Comparator #(.mode("unsigned"), .width(7)) comparator_23 (
    .a(inst[31:25]), .b(7'b0000001), .eq(comparator_23_eq));  // open: gt, lt
  Comparator #(.mode("unsigned"), .width(3)) comparator_24 (
    .a(inst[14:12]), .b(3'b101), .eq(comparator_24_eq));  // open: gt, lt
  Comparator #(.mode("unsigned"), .width(7)) comparator_25 (
    .a(inst[31:25]), .b(7'b0100000), .eq(comparator_25_eq));  // open: gt, lt
  Multiplexer #(.enable("false"), .width(2)) multiplexer_4 (
    .in0(multiplexer_2_out), .in1(2'b11), .out(WBSel), .sel(WBSel_Imm));
  or or_3 (RegWEn, comparator_7_eq, comparator_8_eq, comparator_9_eq, comparator_10_eq, comparator_11_eq, comparator_12_eq, comparator_13_eq);
  Multiplexer #(.enable("false"), .width(4)) multiplexer_5 (
    .in0(multiplexer_3_out), .in1(4'b1010), .out(multiplexer_5_out), .sel(is_Mul));
  and and_1 (is_Mul, comparator_15_eq, comparator_16_eq, comparator_17_eq);
  and and_2 (is_Sub, comparator_18_eq, comparator_19_eq, comparator_20_eq);
  and and_3 (is_Mulh, comparator_21_eq, comparator_22_eq, comparator_23_eq);
  and and_4 (is_Sra, comparator_24_eq, comparator_25_eq);
  Multiplexer #(.enable("false"), .width(4)) multiplexer_6 (
    .in0(multiplexer_5_out), .in1(4'b1100), .out(multiplexer_6_out), .sel(is_Sub));
  Multiplexer #(.enable("false"), .width(4)) multiplexer_7 (
    .in0(multiplexer_6_out), .in1(4'b1110), .out(multiplexer_7_out), .sel(is_Mulh));
  Multiplexer #(.enable("false"), .width(4)) multiplexer_8 (
    .in0(multiplexer_7_out), .in1(4'b0101), .out(ALUSel_IR), .sel(is_Sra));
  Comparator #(.mode("unsigned"), .width(7)) comparator_26 (
    .a(inst[6:0]), .b(7'b0110011), .eq(comparator_26_eq));  // open: gt, lt
  Comparator #(.mode("unsigned"), .width(7)) comparator_27 (
    .a(inst[6:0]), .b(7'b0010011), .eq(comparator_27_eq));  // open: gt, lt
  Multiplexer #(.enable("false"), .width(4)) multiplexer_9 (
    .in0(4'b0000), .in1(ALUSel_IR), .out(ALUSel), .sel(or_4_out));
  Comparator #(.mode("unsigned"), .width(7)) comparator_28 (.a(inst[6:0]), .b(7'b0100011), .eq(MemRW));  // open: gt, lt
  Comparator #(.mode("unsigned"), .width(7)) comparator_29 (
    .a(inst[6:0]), .b(7'b0010111), .eq(comparator_29_eq));  // open: gt, lt
  Comparator #(.mode("unsigned"), .width(7)) comparator_30 (
    .a(inst[6:0]), .b(7'b0110111), .eq(comparator_30_eq));  // open: gt, lt
  Comparator #(.mode("unsigned"), .width(7)) comparator_31 (
    .a(inst[6:0]), .b(7'b1100011), .eq(ImmSel_B));  // open: gt, lt
  Comparator #(.mode("unsigned"), .width(3)) comparator_32 (
    .a(inst[14:12]), .b(3'b110), .eq(comparator_32_eq));  // open: gt, lt
  Comparator #(.mode("unsigned"), .width(3)) comparator_33 (
    .a(inst[14:12]), .b(3'b111), .eq(comparator_33_eq));  // open: gt, lt
  Comparator #(.mode("unsigned"), .width(7)) comparator_34 (
    .a(inst[6:0]), .b(7'b1101111), .eq(ImmSel_J));  // open: gt, lt
  Comparator #(.mode("unsigned"), .width(7)) comparator_35 (
    .a(inst[6:0]), .b(7'b1110011), .eq(comparator_35_eq));  // open: gt, lt
  Comparator #(.mode("unsigned"), .width(3)) comparator_36 (
    .a(inst[14:12]), .b(3'b101), .eq(comparator_36_eq));  // open: gt, lt
  or or_4 (or_4_out, comparator_26_eq, comparator_27_eq);
  or or_5 (or_5_out, comparator_32_eq, comparator_33_eq);
  Comparator #(.mode("unsigned"), .width(7)) comparator_37 (
    .a(inst[6:0]), .b(7'b0000011), .eq(comparator_37_eq));  // open: gt, lt
  Comparator #(.mode("unsigned"), .width(7)) comparator_38 (
    .a(inst[6:0]), .b(7'b0010011), .eq(comparator_38_eq));  // open: gt, lt
  Comparator #(.mode("unsigned"), .width(7)) comparator_39 (
    .a(inst[6:0]), .b(7'b0100011), .eq(comparator_39_eq));  // open: gt, lt
  Comparator #(.mode("unsigned"), .width(7)) comparator_40 (
    .a(inst[6:0]), .b(7'b1100011), .eq(comparator_40_eq));  // open: gt, lt
  Comparator #(.mode("unsigned"), .width(7)) comparator_41 (
    .a(inst[6:0]), .b(7'b0010111), .eq(comparator_41_eq));  // open: gt, lt
  Comparator #(.mode("unsigned"), .width(7)) comparator_42 (
    .a(inst[6:0]), .b(7'b0110111), .eq(comparator_42_eq));  // open: gt, lt
  Comparator #(.mode("unsigned"), .width(7)) comparator_43 (
    .a(inst[6:0]), .b(7'b1101111), .eq(comparator_43_eq));  // open: gt, lt
  Comparator #(.mode("unsigned"), .width(7)) comparator_44 (
    .a(inst[6:0]), .b(7'b1100111), .eq(comparator_44_eq));  // open: gt, lt
  or or_6 (ImmSel_U, comparator_29_eq, comparator_30_eq);
  and and_5 (BrUn, ImmSel_B, or_5_out);
  and and_6 (CSRSel, comparator_35_eq, comparator_36_eq);
  or or_7 (BSel, comparator_37_eq, comparator_38_eq, comparator_39_eq, comparator_40_eq, comparator_41_eq, comparator_42_eq, comparator_43_eq, comparator_44_eq);
  Multiplexer #(.enable("false"), .width(3)) multiplexer_10 (
    .in0(3'b000), .in1(3'b001), .out(multiplexer_10_out), .sel(MemRW));
  Multiplexer #(.enable("false"), .width(3)) multiplexer_11 (
    .in0(multiplexer_10_out), .in1(3'b010), .out(multiplexer_11_out), .sel(ImmSel_B));
  Multiplexer #(.enable("false"), .width(3)) multiplexer_12 (
    .in0(multiplexer_11_out), .in1(3'b011), .out(multiplexer_12_out), .sel(ImmSel_U));
  Comparator #(.mode("unsigned"), .width(7)) comparator_45 (
    .a(inst[6:0]), .b(7'b1100011), .eq(comparator_45_eq));  // open: gt, lt
  Comparator #(.mode("unsigned"), .width(3)) comparator_46 (
    .a(inst[14:12]), .b(3'b100), .eq(comparator_46_eq));  // open: gt, lt
  Comparator #(.mode("unsigned"), .width(3)) comparator_47 (
    .a(inst[14:12]), .b(3'b101), .eq(comparator_47_eq));  // open: gt, lt
  Comparator #(.mode("unsigned"), .width(3)) comparator_48 (
    .a(inst[14:12]), .b(3'b110), .eq(comparator_48_eq));  // open: gt, lt
  Comparator #(.mode("unsigned"), .width(3)) comparator_49 (
    .a(inst[14:12]), .b(3'b111), .eq(comparator_49_eq));  // open: gt, lt
  Multiplexer #(.enable("false"), .width(3)) multiplexer_13 (
    .in0(multiplexer_12_out), .in1(3'b100), .out(multiplexer_13_out), .sel(ImmSel_J));
  Comparator #(.mode("unsigned"), .width(7)) comparator_50 (
    .a(inst[6:0]), .b(7'b1100011), .eq(comparator_50_eq));  // open: gt, lt
  Comparator #(.mode("unsigned"), .width(7)) comparator_51 (
    .a(inst[6:0]), .b(7'b0010111), .eq(comparator_51_eq));  // open: gt, lt
  Comparator #(.mode("unsigned"), .width(7)) comparator_52 (
    .a(inst[6:0]), .b(7'b1101111), .eq(comparator_52_eq));  // open: gt, lt
  Comparator #(.mode("unsigned"), .width(3)) comparator_53 (
    .a(inst[14:12]), .b(3'b000), .eq(comparator_53_eq));  // open: gt, lt
  Comparator #(.mode("unsigned"), .width(3)) comparator_54 (
    .a(inst[14:12]), .b(3'b001), .eq(comparator_54_eq));  // open: gt, lt
  not not_1 (not_1_out, BrLt);
  not not_2 (not_2_out, BrLt);
  and and_7 (and_7_out, comparator_53_eq, BrEq);
  not not_3 (not_3_out, BrEq);
  and and_8 (and_8_out, comparator_46_eq, BrLt);
  and and_9 (and_9_out, not_1_out, comparator_47_eq);
  and and_10 (and_10_out, comparator_48_eq, BrLt);
  and and_11 (and_11_out, not_2_out, comparator_49_eq);
  Multiplexer #(.enable("false"), .width(3)) multiplexer_14 (
    .in0(multiplexer_13_out), .in1(3'b101), .out(ImmSel), .sel(CSRSel));
  or or_8 (ASel, comparator_50_eq, comparator_51_eq, comparator_52_eq);
  and and_12 (and_12_out, not_3_out, comparator_54_eq);
  or or_9 (or_9_out, and_7_out, and_12_out, and_8_out, and_9_out, and_10_out, and_11_out);
  and and_13 (and_13_out, comparator_45_eq, or_9_out);
  Comparator #(.mode("unsigned"), .width(7)) comparator_55 (
    .a(inst[6:0]), .b(7'b1100111), .eq(comparator_55_eq));  // open: gt, lt
  Comparator #(.mode("unsigned"), .width(7)) comparator_56 (
    .a(inst[6:0]), .b(7'b1101111), .eq(comparator_56_eq));  // open: gt, lt
  or or_10 (PCSel, and_13_out, comparator_55_eq, comparator_56_eq);

  // Other names for the same wires on the sheet: ImmSel_CSR = CSRSel; ImmSel_S = MemRW; opcode[6:0] = inst[6:0];
  //   rd[4:0] = inst[11:7]; func3[2:0] = inst[14:12]; rs1[4:0] = inst[19:15]; rs2[4:0] = inst[24:20];
  //   func7[6:0] = inst[31:25]

  // Notes on the sheet:
  //   INPUTS to your circuit
  //   WriteBackSel
  //   CSRWEn
  //   Decode
  //   RegWEn
  //   ALUSel
  //   DON'T CHANGE THE LOCATIONS OF THE INPUTS AND OUTPUTS!
  //   OUTPUT from your circuit
  //   S
  //   U
  //   B
  //   J
  //   CSR
  //   ImmSel
  //   BSel
  //   ASel
  //   PCSel
endmodule
