// Logisim project cpu.circ as structural Verilog: 1 circuit, main circuit cpu
module cpu (
  input  clk,
  input  [31:0] INSTRUCTION,
  input  [31:0] READ_DATA,
  output [31:0] WRITE_ADDRESS,
  output [31:0] PROGRAM_COUNTER,
  output [31:0] ra,
  output [31:0] sp,
  output [31:0] t0,
  output [31:0] t1,
  output [31:0] t2,
  output [31:0] s0,
  output [31:0] s1,
  output [31:0] a0,
  output [31:0] tohost,
  output [3:0] WRITE_ENABLE,
  output [31:0] WRITE_DATA
);

  wire ASel, BrEq, BrLt, BrUn, BSel, comparator_1_eq, comparator_2_eq, comparator_3_eq, comparator_4_eq,
       comparator_5_eq, comparator_6_eq, comparator_7_eq, comparator_8_eq, CSRSel, CSRWen, LB, LH, LW, MemRW,
       PCSel, RegWEn, SB, SH, SW;
  wire [1:0] result, WBSel;
  wire [2:0] func3, ImmSel;
  wire [3:0] ALUSel, multiplexer_7_out, multiplexer_8_out;
  wire [6:0] func7;
  wire [15:0] bit_extender_1_out, multiplexer_9_out;
  wire [24:0] INSTRUCTION_1;
  wire [31:0] A, adder_1_out, B, bit_extender_2_out, CSR_din, imm, multiplexer_1_out, multiplexer_2_out, PC4,
       PROGRAM_COUNTER_1, read_1, READ_DATA1, writeback;

  Adder #(.width(32)) adder_1 (.a(PROGRAM_COUNTER), .b(32'h4), .out(adder_1_out));  // open: cin, cout
  Multiplexer #(.enable("false"), .width(32)) multiplexer_1 (
    .in0(adder_1_out), .in1({WRITE_ADDRESS[31:2], result}), .out(multiplexer_1_out), .sel(PCSel));
  Register #(.width(32)) PC (.D(multiplexer_1_out), .en(1'b1), .clk(clk), .Q(PROGRAM_COUNTER));  // open: clr
  Multiplexer #(.enable("false"), .width(32)) multiplexer_2 (
    .in0(INSTRUCTION), .in1(32'h13), .out(multiplexer_2_out), .sel(PCSel));
  Register #(.width(64)) IF_ID (
    .D({multiplexer_2_out, PROGRAM_COUNTER}), .en(1'b1), .clk(clk),
    .Q({func7, INSTRUCTION_1[24:15], func3, INSTRUCTION_1[11:0], PROGRAM_COUNTER_1}));  // open: clr
  control_logic control_logic_1 (
    .CSRWen(CSRWen), .PCSel(PCSel), .RegWEn(RegWEn), .ImmSel(ImmSel), .BrUn(BrUn), .ASel(ASel), .BSel(BSel),
    .ALUSel(ALUSel), .MemRW(MemRW), .WBSel(WBSel), .CSRSel(CSRSel),
    .inst({func7, INSTRUCTION_1[24:15], func3, INSTRUCTION_1[11:0]}), .BrEq(BrEq), .BrLt(BrLt));
  imm_gen imm_gen_1 (.inst({func7, INSTRUCTION_1[24:15], func3, INSTRUCTION_1[11:0]}), .ImmSel(ImmSel), .imm(imm));
  regfile regfile_1 (
    .rs1(INSTRUCTION_1[19:15]), .rs2(INSTRUCTION_1[24:20]), .rd(INSTRUCTION_1[11:7]), .Write_Data(writeback),
    .RegWEn(RegWEn), .clk(clk), .ra(ra), .sp(sp), .t0(t0), .t1(t1), .t2(t2), .s0(s0), .s1(s1), .a0(a0),
    .Read_Data_1(read_1), .Read_Data_2(WRITE_DATA));
  branch_comp branch_comp_1 (.rs1(read_1), .rs2(WRITE_DATA), .BrUn(BrUn), .BrEq(BrEq), .BrLt(BrLt));
  Multiplexer #(.enable("false"), .width(32)) multiplexer_3 (.in0(read_1), .in1(imm), .out(CSR_din), .sel(CSRSel));
  alu alu_1 (.Result({WRITE_ADDRESS[31:2], result}), .A(A), .B(B), .ALUSel(ALUSel));
  csr csr_1 (.CSR_address(12'h51e), .CSR_din(CSR_din), .CSR_WE(CSRWen), .clk(clk), .tohost(tohost));
  Multiplexer #(.enable("false"), .width(32)) multiplexer_4 (
    .in0(read_1), .in1(PROGRAM_COUNTER_1), .out(A), .sel(ASel));
  Multiplexer #(.enable("false"), .width(32)) multiplexer_5 (.in0(WRITE_DATA), .in1(imm), .out(B), .sel(BSel));
  Multiplexer #(.enable("false"), .select(2), .width(32)) multiplexer_6 (
    .in0(READ_DATA1), .in1({WRITE_ADDRESS[31:2], result}), .in2(PC4), .in3(imm), .out(writeback), .sel(WBSel));
  Multiplexer #(.enable("false"), .width(4)) multiplexer_7 (
    .in0(4'b0000), .in1(4'b0001), .out(multiplexer_7_out), .sel(SB));
  Multiplexer #(.enable("false"), .width(4)) multiplexer_8 (
    .in0(multiplexer_7_out), .in1(4'b0011), .out(multiplexer_8_out), .sel(SH));
  Comparator #(.mode("unsigned"), .width(7)) comparator_1 (
    .a(INSTRUCTION_1[6:0]), .b(7'b0000011), .eq(comparator_1_eq));  // open: gt, lt
  Comparator #(.mode("unsigned"), .width(3)) comparator_2 (
    .a(func3), .b(3'b000), .eq(comparator_2_eq));  // open: gt, lt
  Comparator #(.mode("unsigned"), .width(3)) comparator_3 (
    .a(func3), .b(3'b001), .eq(comparator_3_eq));  // open: gt, lt
  Comparator #(.mode("unsigned"), .width(3)) comparator_4 (
    .a(func3), .b(3'b010), .eq(comparator_4_eq));  // open: gt, lt
  assign bit_extender_1_out = {{8{1'b0}}, READ_DATA[7:0]};  // Bit_Extender bit_extender_1
  Multiplexer #(.enable("false"), .width(16)) multiplexer_9 (
    .in0(bit_extender_1_out), .in1(READ_DATA[15:0]), .out(multiplexer_9_out), .sel(LH));
  Multiplexer #(.enable("false"), .width(4)) multiplexer_10 (
    .in0(multiplexer_8_out), .in1(4'b1111), .out(WRITE_ENABLE), .sel(SW));
  and and_1 (LB, comparator_1_eq, comparator_2_eq);
  and and_2 (LH, comparator_1_eq, comparator_3_eq);
  and and_3 (LW, comparator_1_eq, comparator_4_eq);
  assign bit_extender_2_out = {{16{1'b0}}, multiplexer_9_out};  // Bit_Extender bit_extender_2
  Adder #(.width(32)) adder_2 (.a(PROGRAM_COUNTER_1), .b(32'h4), .out(PC4));  // open: cin, cout
  Multiplexer #(.enable("false"), .width(32)) multiplexer_11 (
    .in0(bit_extender_2_out), .in1(READ_DATA), .out(READ_DATA1), .sel(LW));
  Comparator #(.mode("unsigned"), .width(7)) comparator_5 (
    .a(INSTRUCTION_1[6:0]), .b(7'b0100011), .eq(comparator_5_eq));  // open: gt, lt
  Comparator #(.mode("unsigned"), .width(3)) comparator_6 (
    .a(func3), .b(3'b000), .eq(comparator_6_eq));  // open: gt, lt
  Comparator #(.mode("unsigned"), .width(3)) comparator_7 (
    .a(func3), .b(3'b001), .eq(comparator_7_eq));  // open: gt, lt
  Comparator #(.mode("unsigned"), .width(3)) comparator_8 (
    .a(func3), .b(3'b010), .eq(comparator_8_eq));  // open: gt, lt
  and and_4 (SB, comparator_5_eq, comparator_6_eq);
  and and_5 (SH, comparator_5_eq, comparator_7_eq);
  and and_6 (SW, comparator_5_eq, comparator_8_eq);

  assign WRITE_ADDRESS[1:0] = 2'b00;

  // Other names for the same wires on the sheet: opcode[6:0] = INSTRUCTION_1[6:0]; rd[4:0] = INSTRUCTION_1[11:7];
  //   INSTRUCTION_1 (some bits) = {func7, func3}; rs1[4:0] = INSTRUCTION_1[19:15]; rs2[4:0] = INSTRUCTION_1[24:20];
  //   read_2[31:0] = WRITE_DATA; result[31:2] = WRITE_ADDRESS[31:2]

  // Notes on the sheet:
  //   Output to IMEM
  //   Now just split instruction based on addi
  //   IMEM (do **NOT** move this)
  //   Inputs from IMEM
  //   It is OK to move the PC, RegFile, ALU, MEM, Branch Comp, Imm Gen, and Control Logic to wherever is most convenient for you when constructing your CPU, and to delete this text
  //   Inputs/Outputs for testing. Do **NOT** move these.
  //   Outputs To DMEM
  //   DMEM (do **NOT** move this)
  //   Inputs From DMEM
endmodule
