// Logisim project regfile.circ as structural Verilog: 1 circuit, main circuit regfile
module regfile (
  input  [4:0] rs1,
  input  [4:0] rs2,
  input  [4:0] rd,
  input  [31:0] Write_Data,
  input  RegWEn,
  input  clk,
  output [31:0] ra,
  output [31:0] sp,
  output [31:0] t0,
  output [31:0] t1,
  output [31:0] t2,
  output [31:0] s0,
  output [31:0] s1,
  output [31:0] a0,
  output [31:0] Read_Data_1,
  output [31:0] Read_Data_2
);

  wire we14, we15, we16, we17, we18, we19, we20, we21, we22, we23, we24, we25, we26, we27, we28, we29, we30,
       we31, write_en_0, write_en_1, write_en_2, write_en_3, write_en_4, write_en_5, write_en_6, write_en_7,
       write_en_8, write_en_9, write_en_10, write_en_11, write_en_12, write_en_13;
  wire [31:0] read_0, read_3, read_4, read_11, read_12, read_13, read_14, read_15, read_16, read_17, read_18,
       read_19, read_20, read_21, read_22, read_23, read_24, read_25, read_26, read_27, read_28, read_29,
       read_30, read_31;

  Register #(.width(32)) x0 (.D(Write_Data), .en(1'b0), .clk(clk), .Q(read_0));  // open: clr
  Register #(.width(32)) register_1 (.D(Write_Data), .en(write_en_1), .clk(clk), .Q(ra));  // open: clr
  Register #(.width(32)) register_2 (.D(Write_Data), .en(write_en_2), .clk(clk), .Q(sp));  // open: clr
  Register #(.width(32)) register_3 (.D(Write_Data), .en(write_en_3), .clk(clk), .Q(read_3));  // open: clr
  Register #(.width(32)) register_4 (.D(Write_Data), .en(write_en_4), .clk(clk), .Q(read_4));  // open: clr
  Register #(.width(32)) register_5 (.D(Write_Data), .en(write_en_5), .clk(clk), .Q(t0));  // open: clr
  Register #(.width(32)) register_6 (.D(Write_Data), .en(write_en_6), .clk(clk), .Q(t1));  // open: clr
  Register #(.width(32)) register_7 (.D(Write_Data), .en(write_en_7), .clk(clk), .Q(t2));  // open: clr
  Register #(.width(32)) register_8 (.D(Write_Data), .en(write_en_8), .clk(clk), .Q(s0));  // open: clr
  Register #(.width(32)) register_9 (.D(Write_Data), .en(write_en_9), .clk(clk), .Q(s1));  // open: clr
  Register #(.width(32)) register_10 (.D(Write_Data), .en(write_en_10), .clk(clk), .Q(a0));  // open: clr
  Register #(.width(32)) register_11 (.D(Write_Data), .en(write_en_11), .clk(clk), .Q(read_11));  // open: clr
  Register #(.width(32)) register_12 (.D(Write_Data), .en(write_en_12), .clk(clk), .Q(read_12));  // open: clr
  Register #(.width(32)) register_13 (.D(Write_Data), .en(write_en_13), .clk(clk), .Q(read_13));  // open: clr
  Register #(.width(32)) register_14 (.D(Write_Data), .en(we14), .clk(clk), .Q(read_14));  // open: clr
  Register #(.width(32)) register_15 (.D(Write_Data), .en(we15), .clk(clk), .Q(read_15));  // open: clr
  Register #(.width(32)) register_16 (.D(Write_Data), .en(we16), .clk(clk), .Q(read_16));  // open: clr
  Register #(.width(32)) register_17 (.D(Write_Data), .en(we17), .clk(clk), .Q(read_17));  // open: clr
  Register #(.width(32)) register_18 (.D(Write_Data), .en(we18), .clk(clk), .Q(read_18));  // open: clr
  Register #(.width(32)) register_19 (.D(Write_Data), .en(we19), .clk(clk), .Q(read_19));  // open: clr
  Register #(.width(32)) register_20 (.D(Write_Data), .en(we20), .clk(clk), .Q(read_20));  // open: clr
  Register #(.width(32)) register_21 (.D(Write_Data), .en(we21), .clk(clk), .Q(read_21));  // open: clr
  Register #(.width(32)) register_22 (.D(Write_Data), .en(we22), .clk(clk), .Q(read_22));  // open: clr
  Register #(.width(32)) register_23 (.D(Write_Data), .en(we23), .clk(clk), .Q(read_23));  // open: clr
  Register #(.width(32)) register_24 (.D(Write_Data), .en(we24), .clk(clk), .Q(read_24));  // open: clr
  Register #(.width(32)) register_25 (.D(Write_Data), .en(we25), .clk(clk), .Q(read_25));  // open: clr
  Register #(.width(32)) register_26 (.D(Write_Data), .en(we26), .clk(clk), .Q(read_26));  // open: clr
  Register #(.width(32)) register_27 (.D(Write_Data), .en(we27), .clk(clk), .Q(read_27));  // open: clr
  Register #(.width(32)) register_28 (.D(Write_Data), .en(we28), .clk(clk), .Q(read_28));  // open: clr
  Register #(.width(32)) register_29 (.D(Write_Data), .en(we29), .clk(clk), .Q(read_29));  // open: clr
  Register #(.width(32)) register_30 (.D(Write_Data), .en(we30), .clk(clk), .Q(read_30));  // open: clr
  Register #(.width(32)) register_31 (.D(Write_Data), .en(we31), .clk(clk), .Q(read_31));  // open: clr
  Demultiplexer #(.enable("false"), .select(5)) demultiplexer_1 (
    .out0(write_en_0), .out1(write_en_1), .out2(write_en_2), .out3(write_en_3), .out4(write_en_4),
    .out5(write_en_5), .out6(write_en_6), .out7(write_en_7), .out8(write_en_8), .out9(write_en_9),
    .out10(write_en_10), .out11(write_en_11), .out12(write_en_12), .out13(write_en_13), .out14(we14),
    .out15(we15), .out16(we16), .out17(we17), .out18(we18), .out19(we19), .out20(we20), .out21(we21),
    .out22(we22), .out23(we23), .out24(we24), .out25(we25), .out26(we26), .out27(we27), .out28(we28),
    .out29(we29), .out30(we30), .out31(we31), .in(RegWEn), .sel(rd));
  Multiplexer #(.enable("false"), .select(5), .width(32)) multiplexer_1 (
    .in0(read_0), .in1(ra), .in2(sp), .in3(read_3), .in4(read_4), .in5(t0), .in6(t1), .in7(t2), .in8(s0),
    .in9(s1), .in10(a0), .in11(read_11), .in12(read_12), .in13(read_13), .in14(read_14), .in15(read_15),
    .in16(read_16), .in17(read_17), .in18(read_18), .in19(read_19), .in20(read_20), .in21(read_21),
    .in22(read_22), .in23(read_23), .in24(read_24), .in25(read_25), .in26(read_26), .in27(read_27),
    .in28(read_28), .in29(read_29), .in30(read_30), .in31(read_31), .out(Read_Data_1), .sel(rs1));
  Multiplexer #(.enable("false"), .select(5), .width(32)) multiplexer_2 (
    .in0(read_0), .in1(ra), .in2(sp), .in3(read_3), .in4(read_4), .in5(t0), .in6(t1), .in7(t2), .in8(s0),
    .in9(s1), .in10(a0), .in11(read_11), .in12(read_12), .in13(read_13), .in14(read_14), .in15(read_15),
    .in16(read_16), .in17(read_17), .in18(read_18), .in19(read_19), .in20(read_20), .in21(read_21),
    .in22(read_22), .in23(read_23), .in24(read_24), .in25(read_25), .in26(read_26), .in27(read_27),
    .in28(read_28), .in29(read_29), .in30(read_30), .in31(read_31), .out(Read_Data_2), .sel(rs2));

  // Other names for the same wires on the sheet: read_1[31:0] = ra; read_2[31:0] = sp; read_5[31:0] = t0;
  //   read_6[31:0] = t1; read_7[31:0] = t2; read_8[31:0] = s0; read_9[31:0] = s1; read_10[31:0] = a0;
  //   read_data1[31:0] = Read_Data_1; read_data2[31:0] = Read_Data_2; read_reg1[4:0] = rs1; read_reg2[4:0] = rs2;
  //   write_en = RegWEn; write_en_14 = we14; write_en_15 = we15; write_en_16 = we16; write_en_17 = we17;
  //   write_en_18 = we18; write_en_19 = we19; write_en_20 = we20; write_en_21 = we21; write_en_22 = we22;
  //   write_en_23 = we23; write_en_24 = we24; write_en_25 = we25; write_en_26 = we26; write_en_27 = we27;
  //   write_en_28 = we28; write_en_29 = we29; write_en_30 = we30; write_en_31 = we31; write_reg[4:0] = rd

  // Notes on the sheet:
  //   INPUTS to your circuit
  //   DON'T CHANGE THE LOCATIONS OF THE INPUTS AND OUTPUTS!
  //   These are DEBUG/TEST outputs from your circuit.
  //   OUTPUTS from your circuit
endmodule
